// Logisim project FPA.circ as structural Verilog: 2 circuits, main circuit main
module main (
  input  [31:0] A,
  input  [31:0] B,
  output OverFlow,
  output UnderFlow,
  output [8:0] Larger_Exponent,
  output [31:0] Output
);

  wire inputhandler_1_larger_sign, inputhandler_1_smaller_sign, main_1_outputsign;
  wire [8:0] main_2_normalizedexponent, rounded_normalizer_1_normalized_exponent;
  wire [31:0] inputhandler_1_larger_fraction, inputhandler_1_shifted_small_fraction,
       main_1_output_of_whole_adder, main_2_normalizedsignificand, main_3_rounded_significant,
       rounded_normalizer_1_normalized_significand;

  InputHandler inputhandler_1 (
    .InputA(A), .InputB(B), .Exponant_Difference(Larger_Exponent),
    .Larger_Fraction(inputhandler_1_larger_fraction), .Larger_Sign(inputhandler_1_larger_sign),
    .Shifted_Small_Fraction(inputhandler_1_shifted_small_fraction), .Smaller_sign(inputhandler_1_smaller_sign));  // open: out_5, Larger_Exponant, Samller_Fraction
  Adder_main main_1 (
    .A(inputhandler_1_larger_fraction), .B(inputhandler_1_shifted_small_fraction),
    .SIGNA(inputhandler_1_larger_sign), .SIGNB(inputhandler_1_smaller_sign),
    .OUTPUT_OF_WHOLE_ADDER(main_1_output_of_whole_adder), .OUTPUTSIGN(main_1_outputsign));  // open: out_5
  Normalizer_main main_2 (
    .Exponent_Input(Larger_Exponent), .Significand_Input(main_1_output_of_whole_adder),
    .UnderFlow(UnderFlow), .OverFlow(OverFlow), .NormalizedExponent(main_2_normalizedexponent),
    .NormalizedSignificand(main_2_normalizedsignificand));
  Rounder_main main_3 (.in_1(main_2_normalizedsignificand), .ROUNDED_SIGNIFICANT(main_3_rounded_significant));
  Rounded_Normalizer rounded_normalizer_1 (
    .Exponent_Input(main_2_normalizedexponent), .Significand_Input(main_3_rounded_significant),
    .Normalized_Exponent(rounded_normalizer_1_normalized_exponent),
    .Normalized_Significand(rounded_normalizer_1_normalized_significand));  // open: Overflow
  Output_Handler output_handler_1 (
    .Significand(rounded_normalizer_1_normalized_significand[29:8]),
    .Exponent(rounded_normalizer_1_normalized_exponent), .Sign(main_1_outputsign), .Output(Output));
endmodule

module Output_Handler (
  input  [21:0] Significand,
  input  [8:0] Exponent,
  input  Sign,
  output [31:0] Output
);


  assign Output = {Sign, Exponent, Significand};
endmodule
